# Fritzing sketch speaker (saved by Fritzing 1.0.5)
breadboards: 1

parts:
  Part1 = Arduino Uno (Rev3)
  SP1 = SPEAKER [package=pcb_mount_speaker]
  S1 = Pushbutton [package="[THT]"]

nets:
  N1: Part1.D9_PWM, SP1.-
  N2: Part1.GND, SP1.+, S1.Pin_3, S1.Pin_4
  N3: Part1.RESET, S1.Pin_1, S1.Pin_2
